# Fritzing sketch envinfo_client_nodemcu (saved by Fritzing 0.9.3b)
breadboards: 1

parts:
  U1 = NodeMCU V3.0
  DHT1 = DHT11 Humitidy and Temperature Sensor
  R1 = Photocell (LDR) [package=THT]
  R2 = Resistor [tolerance=±5% resistance=220 package=THT]

nets:
  N1: U1.D1, DHT1.DATA
  3V3: U1.3V3, DHT1.VDD, R2.Pin_0
  N2: U1.GND#6, U1.GND#13, U1.GND#16, U1.GND#33, DHT1.GND, R1.pin_0
  N3: U1.A0, R1.pin_1, R2.Pin_1

custom parts:
  NodeMCU V3.0: ESP8266 based NodeMCU
  DHT11 Humitidy and Temperature Sensor: DHT11 Humidity and Temperature Sensor
